# Fritzing sketch canBus Shieldv4 (saved by Fritzing 0.9.1b)
circuit board: 6.9215cm x 5.33756cm
breadboards: 1

parts:
  MCP2515 = IC, DIP package, 18 pins [chip_label=MCP2515]
  OSC = Resonator [frequency="16 Mhz" package=THT]
  C1 = Ceramic Capacitor [capacitance=100nF package="200 mil [THT, multilayer]"]
  C2 = Ceramic Capacitor [capacitance=100nF package="200 mil [THT, multilayer]"]
  C3 = Ceramic Capacitor [capacitance=100nF package="200 mil [THT, multilayer]"]
  MCP2551 = IC, DIP package, 8 pins [chip_label=IC]
  R1 = Resistor [tolerance=±5% resistance=330 package=THT]
  R2 = Resistor [tolerance=±5% resistance=330 package=THT]
  R3 = Resistor [tolerance=±5% resistance=4.7k package=THT]
  J1 = female pin header, 4 pins [form="♀ (female)"]
  R4 = Resistor [tolerance=±5% resistance=330 package=THT]
  R5 = Resistor [tolerance=±5% resistance=330 package=THT]
  J2 = female pin header, 4 pins [form="♀ (female)"]
  1N4001 = Schottky Diode [part_number=1N4001 package="300 mil [THT]"]
  LED2 = LED - 3mm [color="Red (633nm)" package="3 mm [THT]"]
  LED1 = LED - 3mm [color="Red (633nm)" package="3 mm [THT]"]
  LED3 = LED - 3mm [color="Red (633nm)" package="3 mm [THT]"]
  LED4 = LED - 3mm [color="Red (633nm)" package="3 mm [THT]"]
  J3 = female pin header, 2 pins [form="♀ (female)"]
  DB9 = DB9 Connector [package=db9]
  Pad1 = Pad [width=1.24881114410336 height=0.662955972465117 connect=center]
  Pad2 = Pad [width=1.24881114410336 height=0.662955972465117 connect=center]
  J4 = double row female pin header, 6 pins [form="♀ (female)"]  # not connected
  Part1 = Arduino Uno (Rev3)
  Pad3 = Pad [width=1.24881114410336 height=0.662955972465117 connect=center]
  C4 = Ceramic Capacitor [capacitance=100nF voltage=10V package="200 mil [THT, multilayer]"]
  R6 = Temperature Sensor (Thermistor) [thermistor_type=NTC package=THT]
  Pad4 = Pad [width=1.24881114410336 height=0.662955972465117 connect=center]
  Pad5 = Pad [width=1.24881114410336 height=0.662955972465117 connect=center]
  Pad6 = Pad [width=1.24881114410336 height=0.662955972465117 connect=center]
  Pad7 = Pad [width=1.24881114410336 height=0.662955972465117 connect=center]
  Pad8 = Pad [width=1.24881114410336 height=0.662955972465117 connect=center]
  Pad9 = Pad [width=1.24881114410336 height=0.662955972465117 connect=center]

nets:
  N1: MCP2515.pin1, MCP2551.pin1, LED3.cathode
  N2: MCP2515.pin2, MCP2551.pin4, LED4.cathode
  N3: MCP2515.pin3, J1.pin4
  N4: MCP2515.pin4, J1.pin3
  N5: MCP2515.pin5, J1.pin2
  N6: MCP2515.pin6, J1.pin1
  N7: MCP2515.pin7, OSC.0, C2.0
  N8: MCP2515.pin8, OSC.1, C1.0
  N9: MCP2515.pin9, C1.1, C2.1, C3.0, MCP2551.pin2, R3.Pin_0, J2.pin2, DB9.2, Part1.GND, C4.1
  N10: MCP2515.pin10, LED1.cathode, J3.pin1
  N11: MCP2515.pin11, LED2.cathode, J3.pin2
  N12: MCP2515.pin12, Part1.D3_PWM, Pad6.pad, Pad7.pad
  N13: MCP2515.pin13, Part1.D13/SCK
  N14: MCP2515.pin14, Part1.D11_PWM/MOSI
  N15: MCP2515.pin15, Part1.D12/MISO
  N16: MCP2515.pin16, Pad2.pad, Part1.D10_PWM/SS, Pad3.pad
  N17: MCP2515.pin17, Part1.D2, Pad4.pad, Pad8.pad, Pad9.pad
  N18: MCP2515.pin18, C3.1, MCP2551.pin3, R1.Pin_1, R2.Pin_1, R4.Pin_1, R5.Pin_1, Part1.5V, Pad5.pad
  N19: MCP2551.pin6, J2.pin4, DB9.5
  N20: MCP2551.pin7, J2.pin3, DB9.3
  N21: MCP2551.pin8, R3.Pin_1
  N22: R1.Pin_0, LED2.anode
  N23: R2.Pin_0, LED1.anode
  N24: R4.Pin_0, LED4.anode
  N25: R5.Pin_0, LED3.anode
  N26: J2.pin1, 1N4001.cathode, Part1.VIN, C4.0
  N27: 1N4001.anode, R6.pin_1
  N28: DB9.9, R6.pin_0
  N29: Pad1.pad, Part1.D9_PWM

notes:
  ARDUINO
  CAN BUS SHIELD
  SCooper
  TX
  RX
  330R
  4.7K
  100nF
  15pF
  1N4001
  Vin
  MCP2551
  MCP2515
  Gnd
  CanL
  CanH
  RX1
  RX0
  OSC
  CLK
  TX0
  TX1
  TX2
  22uF
  NTC
  6ohm NTC for inrush current limiting
